# Fritzing sketch Circuit diagram (saved by Fritzing 0.9.3b)
breadboards: 1

parts:
  Part1 = Arduino Mega 2560 (Rev3)
  Part2 = Arduino Uno (Rev3) - ICSP
  LCD1 = LCD screen
  Matrix_keypad1 = KEYPAD 4x4
  R2 = Trimmer Potentiometer [maximum_resistance=10kΩ package=THT]
  J1 = Piezo Speaker
  R3 = Resistor [tolerance=±5% resistance=220 package=THT]
  Sensore_PIR_HC-SR501 = HC-SR501 Body Sensor Module

nets:
  N1: Part1.D10_PWM, Sensore_PIR_HC-SR501.OUT
  N2: Part1.D9_PWM, Part2.D9_PWM
  N3: Part1.D8_PWM, Part2.D8
  5V: Part1.5V, Part2.5V, LCD1.VDD, R2.leg2, R3.Pin_0, Sensore_PIR_HC-SR501.VCC
  GND: Part1.GND, Part2.GND, LCD1.VSS, LCD1.LED-, R2.leg1, J1.pin1, Sensore_PIR_HC-SR501.GND
  N4: Part1.D0_RX0, Matrix_keypad1.row4
  N5: Part1.D1_TX0, Matrix_keypad1.row3
  N6: Part1.D2_PWM, Matrix_keypad1.row2
  N7: Part1.D3_PWM, Matrix_keypad1.row1
  N8: Part1.D4_PWM, Matrix_keypad1.col4
  N9: Part1.D5_PWM, Matrix_keypad1.col3
  N10: Part1.D6_PWM, Matrix_keypad1.col2
  N11: Part1.D7_PWM, Matrix_keypad1.col1
  N12: Part2.D11_PWM/MOSI, LCD1.E
  N13: Part2.D12/MISO, LCD1.RS
  N14: Part2.D2, J1.pin2
  N15: Part2.D3_PWM, LCD1.DB7
  N16: Part2.D4, LCD1.DB6
  N17: Part2.D5_PWM, LCD1.DB5
  N18: Part2.D6_PWM, LCD1.DB4
  N19: LCD1.V0, R2.wiper
  N20: LCD1.LED+, R3.Pin_1

custom parts:
  KEYPAD 4x4: Matrix keypad 16 buttons, 4 rows x 4 columns
  HC-SR501 Body Sensor Module: Pyroelectric Infrared PIR Motion Sensor Detector Module
